// Logisim project lab6ALU.circ as structural Verilog: 1 circuit, main circuit ALU
// LAB12-ALU
module ALU (
  input  [4:0] in_1,
  input  [4:0] in_2,
  input  [31:0] ALU_Source_1,
  input  [31:0] ALU_Source_2,
  input  [2:0] ALU_Control,
  output [31:0] ALU_Result
);

  wire [4:0] rinput, sinput, t_rinput;
  wire [31:0] \and , \or , rl, rr, sll, sra, srl, t_rl, t_rr, \xor ;

  // Probe on ALU_Source_1
  // Probe on ALU_Source_2
  Shifter #(.width(32)) shifter_1 (.in(ALU_Source_1), .\dist (sinput), .out(sll));
  Shifter #(.width(32), .shift("lr")) shifter_2 (.in(ALU_Source_1), .\dist (sinput), .out(srl));
  Shifter #(.width(32), .shift("ar")) shifter_3 (.in(ALU_Source_1), .\dist (sinput), .out(sra));
  Shifter #(.width(32), .shift("lr")) shifter_4 (.in(ALU_Source_1), .\dist (rinput), .out(t_rl));
  Shifter #(.width(32)) shifter_5 (.in(ALU_Source_1), .\dist (rinput), .out(t_rr));
  assign rl = sll | t_rl;  // OR_Gate or_1, 32 bits wide
  assign rr = srl | t_rr;  // OR_Gate or_2, 32 bits wide
  assign \and  = ALU_Source_1 & ALU_Source_2;  // AND_Gate and_1, 32 bits wide
  assign \or  = ALU_Source_1 | ALU_Source_2;  // OR_Gate or_3, 32 bits wide
  Bit_Extender #(.in_width(32), .out_width(5)) bit_extender_1 (.in(ALU_Source_2), .out(sinput));
  Subtractor #(.width(5)) subtractor_1 (.a(in_1), .b(sinput), .out(t_rinput));  // open: bin, bout
  Adder #(.width(5)) adder_1 (.a(t_rinput), .b(in_2), .out(rinput));  // open: cin, cout
  assign \xor  = ALU_Source_1 ^ ALU_Source_2;  // XOR_Gate xor_1, 32 bits wide
  // Probe on ALU_Result
  Multiplexer #(.select(3), .width(32)) multiplexer_1 (
    .in0(sll), .in1(srl), .in2(sra), .in3(rl), .in4(rr), .in5(\and ), .in6(\or ), .in7(\xor ),
    .out(ALU_Result), .sel(ALU_Control));  // open: en

  // Other names for the same wires on the sheet: control[2:0] = ALU_Control; result[31:0] = ALU_Result;
  //   source1[31:0] = ALU_Source_1; source2[31:0] = ALU_Source_2

  // Notes on the sheet:
  //   DO NOT CROSS WIRES
  //   OVER THIS BOX
  //   DO NOT CROSS WIRES
  //   OVER THIS BOX
  //   COMPUTE ALL POSSIBLE OPERATIONS
  //   * YOUR CIRCUIT HERE *
  //   DO NOT CROSS WIRES
  //   OVER THIS BOX
  //   DO NOT CROSS WIRES
  //   OVER THIS BOX
  //   SELECT THE REQUESTED RESULT
  //   * YOUR CIRCUIT HERE *
  //   DO NOT CROSS WIRES
  //   OVER THIS BOX
endmodule
