// Logisim project fib15.circ as structural Verilog: 3 circuits, main circuit main
module main (
  output [7:0] out_1,
  output [7:0] out_2
);

  wire clock_1_out;

  Adder adder_1 (.a(8'h1), .b(out_2), .out(out_1));  // open: cin, cout
  Register register_1 (.D(out_1), .Q(out_2), .clk(clock_1_out));  // open: en, clr
  Clock clock_1 (.out(clock_1_out));
  Register register_2 ();  // open: D, en, Q, clk, clr
endmodule

module fib15 (
  output [7:0] out_1
);

  wire clock_1_out, not_1_out;
  wire [7:0] adder_2_out, multiplexer_1_out, register_1_q, register_2_q;

  // Probe on nothing
  // Probe on adder_2_out
  Register register_1 (.D(adder_2_out), .Q(register_1_q), .clk(clock_1_out));  // open: en, clr
  Register register_2 (.D(adder_2_out), .Q(register_2_q), .clk(not_1_out));  // open: en, clr
  not not_1 (not_1_out, clock_1_out);
  Demultiplexer demultiplexer_1 ();  // open: out0, out1, in, sel, en
  Adder adder_1 (.a(register_1_q), .b(register_2_q), .out(out_1));  // open: cin, cout
  Multiplexer #(.width(8)) multiplexer_1 (
    .in0(register_2_q), .in1(register_1_q), .out(multiplexer_1_out), .sel(clock_1_out));  // open: en
  Clock clock_1 (.out(clock_1_out));
  // Probe on out_1
  Adder adder_2 (.a(multiplexer_1_out), .b(out_1), .out(adder_2_out));  // open: cin, cout
  Register register_3 ();  // open: D, en, Q, clk, clr
endmodule

module fib15_r (
  output [7:0] out_1
);

  wire clock_1_out, not_1_out, not_2_out, or_1_out;
  wire [7:0] register_1_q, register_2_q, ri, ro;

  Counter counter_1 ();  // open: load, D, count, Q, carry, clk, clr
  or or_1 (or_1_out, not_1_out, clock_1_out);
  not not_1 (not_1_out, clock_1_out);
  Register register_1 (.D(out_1), .Q(register_1_q), .clk(or_1_out));  // open: en, clr
  Register register_2 (.D(out_1), .Q(register_2_q), .clk(not_2_out));  // open: en, clr
  not not_2 (not_2_out, clock_1_out);
  Clock clock_1 (.out(clock_1_out));
  Adder adder_1 (.a(register_1_q), .b(register_2_q), .out(out_1));  // open: cin, cout
  Register register_3 (.D(ri), .Q(ro), .clk(clock_1_out));  // open: en, clr
  // Probe on out_1
  Subtractor subtractor_1 (.a(ro), .b(8'h1), .out(ri));  // open: bin, bout
endmodule
