// Logisim project cpu.circ as structural Verilog: 4 circuits, main circuit main
module main (
  input  [31:0] INSTRUCTION,
  input  CLOCK,
  output [31:0] FETCH_ADDRESS,
  output [31:0] s0_Value,
  output [31:0] s1_Value,
  output [31:0] s2_Value,
  output [31:0] ra_Value,
  output [31:0] sp_Value
);

  wire ALUSrc, bneSig, bovSig, ExtOp, JalSig, Jump, JumpReg, luiSig, main_2_equal, MemtoReg, MemWr,
       not_1_out, nPC_sel, overflow, pipeline, RegDst, RegWr, ShamtSig, StorePC, Zero;
  wire [3:0] ALUctr;
  wire [4:0] multiplexer_3_out, multiplexer_4_out, rd, rs, rt, shamt;
  wire [5:0] funct, opcode;
  wire [15:0] imm;
  wire [25:0] address;
  wire [31:0] adder_1_out, ALU_result, bit_extender_1_out, bit_extender_2_out, bit_extender_3_out, immet,
       immrt, instr_fetch_unit_1_fetch_addr_2, instruction_t, mem_data, multiplexer_2_out, multiplexer_5_out,
       multiplexer_6_out, multiplexer_9_out, rs_value, rt_value, shifter_1_out, subtractor_1_out, write_data;

  or or_1 (pipeline, nPC_sel, Jump, JumpReg);
  Instruction_Fetch instruction_fetch_1 (
    .instruction(instruction_t), .funct(funct), .shamt(shamt), .rd(rd), .imm(imm), .rt(rt), .rs(rs),
    .address(address), .opcode(opcode));
  Instr_Fetch_Unit instr_fetch_unit_1 (
    .nPC_sel(nPC_sel), .Zero(Zero), .fetch_addr(FETCH_ADDRESS), .imm(imm),
    .fetch_addr_2(instr_fetch_unit_1_fetch_addr_2), .clk(CLOCK), .JumpReg(JumpReg), .rs_value(rs_value),
    .address(address), .Jump(Jump), .overflow(overflow), .bovSig(bovSig));
  Subtractor #(.width(32)) subtractor_1 (
    .a(instr_fetch_unit_1_fetch_addr_2), .b({32{1'b0}}), .out(subtractor_1_out));  // open: bin, bout
  Multiplexer #(.width(32), .enable("false")) multiplexer_1 (
    .in0(instr_fetch_unit_1_fetch_addr_2), .in1(subtractor_1_out), .out(FETCH_ADDRESS), .sel(pipeline));
  Multiplexer #(.width(32), .disabled(0), .enable("false")) multiplexer_2 (
    .in0(INSTRUCTION), .in1({32{1'b0}}), .out(multiplexer_2_out), .sel(pipeline));
  Register #(.width(32)) register_1 (.D(multiplexer_2_out), .Q(instruction_t), .clk(CLOCK));  // open: en, clr
  Multiplexer #(.width(5), .enable("false")) multiplexer_3 (.in0(rt), .in1(rd), .out(multiplexer_3_out), .sel(RegDst));
  Multiplexer #(.width(5), .enable("false")) multiplexer_4 (
    .in0(multiplexer_3_out), .in1({5{1'b1}}), .out(multiplexer_4_out), .sel(JalSig));
  Multiplexer #(.width(32), .enable("false")) multiplexer_5 (
    .in0(write_data), .in1(adder_1_out), .out(multiplexer_5_out), .sel(StorePC));
  regfile_main main_1 (
    .Read_Register_1(rs), .Read_Register_2(rt), .Write_Register(multiplexer_4_out),
    .Write_Data(multiplexer_5_out), .Write_Enable(RegWr), .Clock(CLOCK), .Read_Data_1(rs_value),
    .Read_Data_2(rt_value), .s0_Value(s0_Value), .s1_Value(s1_Value), .s2_Value(s2_Value),
    .ra_Value(ra_Value), .sp_Value(sp_Value));
  Adder #(.width(32)) adder_1 (.a(FETCH_ADDRESS), .b({32{1'b0}}), .out(adder_1_out));  // open: cin, cout
  assign bit_extender_1_out = {{16{1'b0}}, imm};  // Bit_Extender bit_extender_1
  assign bit_extender_2_out = {{16{imm[15]}}, imm};  // Bit_Extender bit_extender_2
  Multiplexer #(.width(32), .enable("false")) multiplexer_6 (
    .in0(rs_value), .in1(bit_extender_3_out), .out(multiplexer_6_out), .sel(ShamtSig));
  assign bit_extender_3_out = {{27{1'b0}}, shamt};  // Bit_Extender bit_extender_3
  Multiplexer #(.width(32), .enable("false")) multiplexer_7 (
    .in0(bit_extender_1_out), .in1(bit_extender_2_out), .out(immet), .sel(ExtOp));
  Multiplexer #(.width(32), .enable("false")) multiplexer_8 (
    .in0(immet), .in1(shifter_1_out), .out(immrt), .sel(luiSig));
  Shifter #(.width(32)) shifter_1 (.in(immet), .\dist (5'b10000), .out(shifter_1_out));
  Multiplexer #(.width(32), .enable("false")) multiplexer_9 (
    .in0(rt_value), .in1(immrt), .out(multiplexer_9_out), .sel(ALUSrc));
  Multiplexer #(.enable("false")) multiplexer_10 (.in0(main_2_equal), .in1(not_1_out), .out(Zero), .sel(bneSig));
  LED led_1 (.in(overflow));
  not not_1 (not_1_out, main_2_equal);
  alu_main main_2 (
    .Switch(ALUctr), .X(multiplexer_6_out), .Equal(main_2_equal), .Result(ALU_result),
    .Signed_Overflow(overflow), .Y(multiplexer_9_out));  // open: in_4
  Controller controller_1 (
    .opcode(opcode), .funct(funct), .RegWrite(RegWr), .RegDst(RegDst), .ExtOp(ExtOp), .JumpReg(JumpReg),
    .ALUSrc(ALUSrc), .MemWrite(MemWr), .StorePC(StorePC), .ShamtSig(ShamtSig), .MemtoReg(MemtoReg),
    .nPC_sel(nPC_sel), .ALUctr(ALUctr), .Jump(Jump), .JalSig(JalSig), .bneSig(bneSig), .bovSig(bovSig),
    .luiSig(luiSig));
  Multiplexer #(.width(32), .enable("false")) multiplexer_11 (
    .in0(ALU_result), .in1(mem_data), .out(write_data), .sel(MemtoReg));
  // mem_main main_3: pin names not known; wires that end beside it: ALU_result, rt_value, MemWr, CLOCK, mem_data

  // Other names for the same wires on the sheet: clk = CLOCK; fetch_addr[31:0] = FETCH_ADDRESS; ra[31:0] = ra_Value;
  //   s0[31:0] = s0_Value; s1[31:0] = s1_Value; s2[31:0] = s2_Value; sp[31:0] = sp_Value

  // Notes on the sheet:
  //   Output
  //   These are outputs/inputs from run.circ
  //   Inputs
  //   These are DEBUG/TEST outputs from your circuit.
endmodule

module Instruction_Fetch (
  input  [31:0] instruction,
  output [5:0] funct,
  output [4:0] shamt,
  output [4:0] rd,
  output [15:0] imm,
  output [4:0] rt,
  output [4:0] rs,
  output [25:0] address,
  output [5:0] opcode
);


  assign address = instruction[25:0];
  assign funct = instruction[5:0];
  assign imm = instruction[15:0];
  assign opcode = instruction[31:26];
  assign rd = instruction[15:11];
  assign rs = instruction[25:21];
  assign rt = instruction[20:16];
  assign shamt = instruction[10:6];
endmodule

module Controller (
  input  [5:0] opcode,
  input  [5:0] funct,
  output RegWrite,
  output RegDst,
  output ExtOp,
  output JumpReg,
  output ALUSrc,
  output MemWrite,
  output StorePC,
  output ShamtSig,
  output MemtoReg,
  output nPC_sel,
  output [3:0] ALUctr,
  output Jump,
  output JalSig,
  output bneSig,
  output bovSig,
  output luiSig
);

  wire add, addi, addiu, addu, \and , andi, beq, bne, bov, j, jal, jalr, jr, lui, lw, \or , ori, r_type, sll,
       slt, slti, sltiu, sltu, sra, srl, sub, subu, sw;

  and and_1 (r_type, ~opcode[5], ~opcode[4], ~opcode[3], ~opcode[2], ~opcode[1], ~opcode[0]);  // AND_Gate
  and u_addi (addi, ~opcode[5], ~opcode[4], opcode[3], ~opcode[2], ~opcode[1], ~opcode[0]);  // AND_Gate
  and u_addiu (addiu, ~opcode[5], ~opcode[4], opcode[3], ~opcode[2], ~opcode[1], opcode[0]);  // AND_Gate
  and u_andi (andi, ~opcode[5], ~opcode[4], opcode[3], opcode[2], ~opcode[1], ~opcode[0]);  // AND_Gate
  and u_beq (beq, ~opcode[5], ~opcode[4], ~opcode[3], opcode[2], ~opcode[1], ~opcode[0]);  // AND_Gate
  and u_bne (bne, ~opcode[5], ~opcode[4], ~opcode[3], opcode[2], ~opcode[1], opcode[0]);  // AND_Gate
  and u_bov (bov, ~opcode[5], ~opcode[4], ~opcode[3], opcode[2], opcode[1], ~opcode[0]);  // AND_Gate
  and u_lui (lui, ~opcode[5], ~opcode[4], opcode[3], opcode[2], opcode[1], opcode[0]);  // AND_Gate
  and u_lw (lw, opcode[5], ~opcode[4], ~opcode[3], ~opcode[2], opcode[1], opcode[0]);  // AND_Gate
  and u_ori (ori, ~opcode[5], ~opcode[4], opcode[3], opcode[2], ~opcode[1], opcode[0]);  // AND_Gate
  and u_slti (slti, ~opcode[5], ~opcode[4], opcode[3], ~opcode[2], opcode[1], ~opcode[0]);  // AND_Gate
  and u_sltiu (sltiu, ~opcode[5], ~opcode[4], opcode[3], ~opcode[2], opcode[1], opcode[0]);  // AND_Gate
  and u_sw (sw, opcode[5], ~opcode[4], opcode[3], ~opcode[2], opcode[1], opcode[0]);  // AND_Gate
  and u_add (add, funct[5], ~funct[4], ~funct[3], r_type, ~funct[2], ~funct[1], ~funct[0]);  // AND_Gate
  and u_addu (addu, funct[5], ~funct[4], ~funct[3], r_type, ~funct[2], ~funct[1], funct[0]);  // AND_Gate
  and and_2 (\and , funct[5], ~funct[4], ~funct[3], r_type, funct[2], ~funct[1], ~funct[0]);  // AND_Gate
  and u_jr (jr, ~funct[5], ~funct[4], funct[3], r_type, ~funct[2], ~funct[1], ~funct[0]);  // AND_Gate
  and u_jalr (jalr, ~funct[5], ~funct[4], funct[3], r_type, ~funct[2], ~funct[1], funct[0]);  // AND_Gate
  and u_or (\or , funct[5], ~funct[4], ~funct[3], r_type, funct[2], ~funct[1], funct[0]);  // AND_Gate
  and u_slt (slt, funct[5], ~funct[4], funct[3], r_type, ~funct[2], funct[1], ~funct[0]);  // AND_Gate
  and u_sltu (sltu, funct[5], ~funct[4], funct[3], r_type, ~funct[2], funct[1], funct[0]);  // AND_Gate
  and u_sll (sll, ~funct[5], ~funct[4], ~funct[3], r_type, ~funct[2], ~funct[1], ~funct[0]);  // AND_Gate
  and u_sra (sra, ~funct[5], ~funct[4], ~funct[3], r_type, ~funct[2], funct[1], funct[0]);  // AND_Gate
  and u_srl (srl, ~funct[5], ~funct[4], ~funct[3], r_type, ~funct[2], funct[1], ~funct[0]);  // AND_Gate
  and u_sub (sub, funct[5], ~funct[4], ~funct[3], r_type, ~funct[2], funct[1], ~funct[0]);  // AND_Gate
  and u_subu (subu, funct[5], ~funct[4], ~funct[3], r_type, ~funct[2], funct[1], funct[0]);  // AND_Gate
  and u_j (j, ~opcode[5], ~opcode[4], ~opcode[3], ~opcode[2], opcode[1], ~opcode[0]);  // AND_Gate
  and u_jal (jal, ~opcode[5], ~opcode[4], ~opcode[3], ~opcode[2], opcode[1], opcode[0]);  // AND_Gate
  or or_2 (JumpReg, jr, jalr);
  or or_3 (StorePC, jalr, jal);
  or or_4 (ShamtSig, sll, sra, srl);
  or or_5 (Jump, j, jal);
  buf or_6 (JalSig, jal);  // OR_Gate
  buf or_7 (bneSig, bne);  // OR_Gate
  buf or_8 (bovSig, bov);  // OR_Gate
  buf or_9 (luiSig, lui);  // OR_Gate
  or or_10 (RegDst, add, addu, \and , jalr, \or , slt, sltu, sll, sra, srl, sub, subu);
  or or_11 (ALUSrc, addi, addiu, andi, lui, lw, ori, sw, slti, sltiu);
  buf or_12 (MemtoReg, lw);  // OR_Gate
  or or_13 (ALUctr[3], \and , \or , slt, sltu, subu, andi, ori, slti, sltiu);
  or or_14 (RegWrite, sltiu, slti, ori, add, addu, \and , jalr, \or , slt, sltu, sll, sra, srl, sub, subu, jal, addi, addiu, andi, lui, lw);
  buf or_15 (MemWrite, sw);  // OR_Gate
  or or_16 (nPC_sel, beq, bne, bov);
  or or_17 (ALUctr[2], add, addu, sltu, sub, addi, addiu, beq, bne, bov, lui, lw, sw, sltiu);
  or or_18 (ExtOp, addi, addiu, lw, sw, slti, sltiu);
  or or_19 (ALUctr[1], addu, \or , slt, sra, sub, addiu, beq, bne, ori, slti);
  or or_20 (ALUctr[0], add, \and , slt, srl, sub, addi, andi, beq, bne, bov, lui, lw, sw, slti);

  // Other names for the same wires on the sheet: ALUOp0 = ALUctr[0]; ALUOp1 = ALUctr[1]; ALUOp2 = ALUctr[2];
  //   ALUOp3 = ALUctr[3]; fu0 = funct[0]; fu1 = funct[1]; fu2 = funct[2]; fu3 = funct[3]; fu4 = funct[4];
  //   fu5 = funct[5]; op0 = opcode[0]; op1 = opcode[1]; op2 = opcode[2]; op3 = opcode[3]; op4 = opcode[4];
  //   op5 = opcode[5]

  // Notes on the sheet:
  //   I-type instruction
  //   R-type instruction
  //   J-type instruction
endmodule

module Instr_Fetch_Unit (
  input  nPC_sel,
  input  Zero,
  input  overflow,
  input  bovSig,
  input  [31:0] fetch_addr,
  input  [31:0] rs_value,
  input  Jump,
  input  clk,
  input  [15:0] imm,
  input  JumpReg,
  input  [25:0] address,
  output [31:0] fetch_addr_2
);

  wire and_1_out, multiplexer_1_out;
  wire [31:0] adder_1_out, adder_2_out, and_2_out, bit_extender_1_out, bit_extender_2_out, multiplexer_2_out,
       multiplexer_3_out, multiplexer_4_out, multiplier_1_out, or_1_out, shifter_1_out;

  Multiplexer #(.enable("false")) multiplexer_1 (.in0(Zero), .in1(overflow), .out(multiplexer_1_out), .sel(bovSig));
  assign bit_extender_1_out = {{16{imm[15]}}, imm};  // Bit_Extender bit_extender_1
  and and_1 (and_1_out, nPC_sel, multiplexer_1_out);
  Multiplier #(.width(32)) multiplier_1 (.a(32'h4), .b(bit_extender_1_out), .out(multiplier_1_out));  // open: cin, cout
  Adder #(.width(32)) adder_1 (.a(32'h4), .b(fetch_addr), .out(adder_1_out));  // open: cin, cout
  Adder #(.width(32)) adder_2 (.a(adder_1_out), .b(multiplier_1_out), .out(adder_2_out));  // open: cin, cout
  assign and_2_out = adder_1_out & 32'hf0000000;  // AND_Gate and_2, 32 bits wide
  Multiplexer #(.width(32), .enable("false")) multiplexer_2 (
    .in0(adder_1_out), .in1(adder_2_out), .out(multiplexer_2_out), .sel(and_1_out));
  assign bit_extender_2_out = {{6{1'b0}}, address};  // Bit_Extender bit_extender_2
  Multiplexer #(.width(32), .enable("false")) multiplexer_3 (
    .in0(multiplexer_2_out), .in1(rs_value), .out(multiplexer_3_out), .sel(JumpReg));
  Shifter #(.width(32)) shifter_1 (.in(bit_extender_2_out), .\dist (5'b00010), .out(shifter_1_out));
  Multiplexer #(.width(32), .enable("false")) multiplexer_4 (
    .in0(multiplexer_3_out), .in1(or_1_out), .out(multiplexer_4_out), .sel(Jump));
  assign or_1_out = shifter_1_out | and_2_out;  // OR_Gate or_1, 32 bits wide
  Register #(.width(32)) PC (.D(multiplexer_4_out), .Q(fetch_addr_2), .clk(clk));  // open: en, clr
endmodule
