// Logisim project alu.circ as structural Verilog: 1 circuit, main circuit main
module main (
  input  [31:0] X,
  input  [31:0] Y,
  input  [3:0] Switch,
  input  [31:0] in_4,
  output Signed_Overflow,
  output Equal,
  output [31:0] Result
);

  wire _0A, _0An, _0Ans, _0As, a_detect, a_ov, and_2_out, and_3_out, and_4_out, and_5_out, neA, neAs, neX,
       neXs, neY, neYs, or_2_out, or_3_out, or_4_out, or_5_out, or_6_out, or_7_out, poA, poAs, poX, poXs,
       poY, poYs, s_detect, s_ov, sltbit, sltbitu;
  wire [4:0] sinput;
  wire [31:0] add, addu, \and , \or , sll, slt, sltu, sra, srl, sub, subu;

  Shifter #(.width(32)) shifter_1 (.in(Y), .\dist (sinput), .out(sll));
  Shifter #(.width(32), .shift("lr")) shifter_2 (.in(Y), .\dist (sinput), .out(srl));
  Shifter #(.width(32), .shift("ar")) shifter_3 (.in(Y), .\dist (sinput), .out(sra));
  assign \or  = X | Y;  // OR_Gate or_1, 32 bits wide
  assign \and  = X & Y;  // AND_Gate and_1, 32 bits wide
  Comparator #(.width(32)) comparator_1 (.a(X), .b({32{1'b0}}), .gt(poX));  // open: eq, lt
  Comparator #(.width(32)) comparator_2 (.a(Y), .b({32{1'b0}}), .gt(poY));  // open: eq, lt
  Comparator #(.width(32)) comparator_3 (.a(add), .b({32{1'b0}}), .eq(_0A), .lt(neA));  // open: gt
  Comparator #(.width(32)) comparator_4 (.a(X), .b({32{1'b0}}), .gt(poXs));  // open: eq, lt
  Comparator #(.width(32)) comparator_5 (.a(Y), .b({32{1'b0}}), .lt(neYs));  // open: gt, eq
  Comparator #(.width(32)) comparator_6 (.a(sub), .b({32{1'b0}}), .gt(poAs), .eq(_0As));  // open: lt
  Bit_Extender #(.in_width(32), .out_width(5)) bit_extender_1 (.in(X), .out(sinput));
  Adder #(.width(32)) adder_1 (.a(X), .b(Y), .out(add), .cout(a_detect));  // open: cin
  Adder #(.width(32)) adder_2 (.a(X), .b(Y), .out(addu));  // open: cin, cout
  Subtractor #(.width(32)) subtractor_1 (.a(X), .b(Y), .out(sub), .bout(s_detect));  // open: bin
  Subtractor #(.width(32)) subtractor_2 (.a(X), .b(Y), .out(subu));  // open: bin, bout
  Comparator #(.width(32)) comparator_7 (.a(X), .b(Y), .eq(Equal));  // open: gt, lt
  Comparator #(.width(32)) comparator_8 (.a(X), .b(Y), .lt(sltbit));  // open: gt, eq
  assign slt = {{31{1'b0}}, sltbit};  // Bit_Extender bit_extender_2
  Comparator #(.width(32), .mode("unsigned")) comparator_9 (.a(X), .b(Y), .lt(sltbitu));  // open: gt, eq
  assign sltu = {{31{1'b0}}, sltbitu};  // Bit_Extender bit_extender_3
  Comparator #(.width(32)) comparator_10 (.a(X), .b({32{1'b0}}), .lt(neX));  // open: gt, eq
  Comparator #(.width(32)) comparator_11 (.a(Y), .b({32{1'b0}}), .lt(neY));  // open: gt, eq
  Comparator #(.width(32)) comparator_12 (.a(add), .b({32{1'b0}}), .gt(poA), .eq(_0An));  // open: lt
  Comparator #(.width(32)) comparator_13 (.a(X), .b({32{1'b0}}), .lt(neXs));  // open: gt, eq
  Comparator #(.width(32)) comparator_14 (.a(Y), .b({32{1'b0}}), .gt(poYs));  // open: eq, lt
  Comparator #(.width(32)) comparator_15 (.a(sub), .b({32{1'b0}}), .eq(_0Ans), .lt(neAs));  // open: gt
  or or_2 (or_2_out, _0A, neA);
  or or_3 (or_3_out, _0An, poA);
  or or_4 (or_4_out, _0As, poAs);
  or or_5 (or_5_out, _0Ans, neAs);
  and and_2 (and_2_out, poX, poY, a_ov, or_2_out);
  and and_3 (and_3_out, neX, neY, a_ov, or_3_out);
  and and_4 (and_4_out, poXs, neYs, s_ov, or_4_out);
  and and_5 (and_5_out, neXs, poYs, s_ov, or_5_out);
  Multiplexer #(.select(4), .width(32)) multiplexer_1 (
    .in0(sll), .in1(srl), .in2(sra), .in3(in_4), .in4(in_4), .in5(add), .in6(addu), .in7(sub), .in8(subu),
    .in9(\and ), .in10(\or ), .in11(slt), .in12(sltu), .in13(in_4), .in14(in_4), .in15(in_4), .out(Result),
    .sel(Switch));  // open: en
  or or_6 (or_6_out, and_2_out, and_3_out);
  or or_7 (or_7_out, and_4_out, and_5_out);
  Comparator #(.width(4)) comparator_16 (.a(Switch), .b(4'b0101), .eq(a_ov));  // open: gt, lt
  Comparator #(.width(4)) comparator_17 (.a(Switch), .b(4'b0111), .eq(s_ov));  // open: gt, lt
  or or_8 (Signed_Overflow, or_6_out, or_7_out);

  // Other names for the same wires on the sheet: overflow = Signed_Overflow; S[3:0] = Switch; zero[31:0] = in_4

  // Notes on the sheet:
  //   INPUTS to your circuit
  //   DON'T CHANGE THE LOCATIONS OF THE INPUTS AND OUTPUTS!
  //   OUTPUTS from your circuit
endmodule
