// Logisim project regfile.circ as structural Verilog: 4 circuits, main circuit main
module main (
  input  [4:0] Read_Register_1,
  input  [4:0] Read_Register_2,
  input  [4:0] Write_Register,
  input  [31:0] Write_Data,
  input  Write_Enable,
  input  Clock,
  input  [31:0] in_7,
  output [31:0] s0_Value,
  output [31:0] s1_Value,
  output [31:0] s2_Value,
  output [31:0] ra_Value,
  output [31:0] sp_Value,
  output [31:0] Read_Data_1,
  output [31:0] Read_Data_2
);

  wire [31:0] _0, _0_prime, _1, _1_prime, _2, _2_prime, _3, _3_prime, _4, _4_prime, _5, _5_prime, _6,
       _6_prime, _7, _7_prime, _8, _8_prime, _9, _9_prime, _10, _10_prime, _11, _11_prime, _12, _12_prime,
       _13, _13_prime, _14, _14_prime, _15, _15_prime, _16, _17, _18, _19, _19_prime, _20, _20_prime, _21,
       _21_prime, _22, _22_prime, _23, _23_prime, _24, _24_prime, _25, _25_prime, _26, _26_prime, _27,
       _27_prime, _28, _28_prime, _29, _30, _30_prime, _31;

  Demultiplexer #(.select(5), .width(32)) demultiplexer_1 (
    .out0(in_7), .out1(_1), .out2(_2), .out3(_3), .out4(_4), .out5(_5), .out6(_6), .out7(_7), .out8(_8),
    .out9(_9), .out10(_10), .out11(_11), .out12(_12), .out13(_13), .out14(_14), .out15(_15), .out16(_16),
    .out17(_17), .out18(_18), .out19(_19), .out20(_20), .out21(_21), .out22(_22), .out23(_23), .out24(_24),
    .out25(_25), .out26(_26), .out27(_27), .out28(_28), .out29(_29), .out30(_30), .out31(_31),
    .in(Write_Data), .sel(Write_Register), .en(Write_Enable));
  Multiplexer #(.select(5), .width(32)) multiplexer_1 (
    .in0(_0_prime), .in1(_1_prime), .in2(_2_prime), .in3(_3_prime), .in4(_4_prime), .in5(_5_prime),
    .in6(_6_prime), .in7(_7_prime), .in8(_8_prime), .in9(_9_prime), .in10(_10_prime), .in11(_11_prime),
    .in12(_12_prime), .in13(_13_prime), .in14(_14_prime), .in15(_15_prime), .in16(s0_Value), .in17(s1_Value),
    .in18(s2_Value), .in19(_19_prime), .in20(_20_prime), .in21(_21_prime), .in22(_22_prime),
    .in23(_23_prime), .in24(_24_prime), .in25(_25_prime), .in26(_26_prime), .in27(_27_prime),
    .in28(_28_prime), .in29(sp_Value), .in30(_30_prime), .in31(ra_Value), .out(Read_Data_1),
    .sel(Read_Register_1));  // open: en
  registers3 Registers (
    .in_1(_0), .in_2(_1), .in_3(_2), .in_4(_3), .in_5(_4), .in_6(_5), .in_7(_6), .in_8(_7), .in_9(_8),
    .in_10(_9), .in_11(_10), .in_12(_11), .in_13(_12), .in_14(_13), .in_15(_14), .in_16(_15), .in_17(_16),
    .in_18(_17), .in_19(_18), .in_20(_19), .in_21(_20), .in_22(_21), .in_23(_22), .in_24(_23), .in_25(_24),
    .in_26(_25), .in_27(_26), .in_28(_27), .in_29(_28), .in_30(_29), .in_31(_30), .in_32(_31), .in_33(Clock),
    .out_34(_0_prime), .out_35(_1_prime), .out_36(_2_prime), .out_37(_3_prime), .out_38(_4_prime),
    .out_39(_5_prime), .out_40(_6_prime), .out_41(_7_prime), .out_42(_8_prime), .out_43(_9_prime),
    .out_44(_10_prime), .out_45(_11_prime), .out_46(_12_prime), .out_47(_13_prime), .out_48(_14_prime),
    .out_49(_15_prime), .out_50(s0_Value), .out_51(s1_Value), .out_52(s2_Value), .out_53(_19_prime),
    .out_54(_20_prime), .out_55(_21_prime), .out_56(_22_prime), .out_57(_23_prime), .out_58(_24_prime),
    .out_59(_25_prime), .out_60(_26_prime), .out_61(_27_prime), .out_62(_28_prime), .out_63(sp_Value),
    .out_64(_30_prime), .out_65(ra_Value));
  Multiplexer #(.select(5), .width(32)) multiplexer_2 (
    .in0(_0_prime), .in1(_1_prime), .in2(_2_prime), .in3(_3_prime), .in4(_4_prime), .in5(_5_prime),
    .in6(_6_prime), .in7(_7_prime), .in8(_8_prime), .in9(_9_prime), .in10(_10_prime), .in11(_11_prime),
    .in12(_12_prime), .in13(_13_prime), .in14(_14_prime), .in15(_15_prime), .in16(s0_Value), .in17(s1_Value),
    .in18(s2_Value), .in19(_19_prime), .in20(_20_prime), .in21(_21_prime), .in22(_22_prime),
    .in23(_23_prime), .in24(_24_prime), .in25(_25_prime), .in26(_26_prime), .in27(_27_prime),
    .in28(_28_prime), .in29(sp_Value), .in30(_30_prime), .in31(ra_Value), .out(Read_Data_2),
    .sel(Read_Register_2));  // open: en

  // Other names for the same wires on the sheet: _16_prime[31:0] = s0_Value; _17_prime[31:0] = s1_Value;
  //   _18_prime[31:0] = s2_Value; _29_prime[31:0] = sp_Value; _31_prime[31:0] = ra_Value; clk = Clock;
  //   read_data1[31:0] = Read_Data_1; read_data2[31:0] = Read_Data_2; read_reg1[4:0] = Read_Register_1;
  //   read_reg2[4:0] = Read_Register_2; write_en = Write_Enable; write_reg[4:0] = Write_Register; zero[31:0] = in_7

  // Notes on the sheet:
  //   INPUTS to your circuit
  //   DON'T CHANGE THE LOCATIONS OF THE INPUTS AND OUTPUTS!
  //   These are DEBUG/TEST outputs from your circuit.
  //   OUTPUTS from your circuit
endmodule

module registers (
);

  wire clk;
  wire [31:0] _0, _0_prime, _1, _1_prime, _2, _2_prime, _3, _3_prime, _4, _4_prime, _5, _5_prime, _6,
       _6_prime, _7, _7_prime, _8, _8_prime, _9, _9_prime, _10, _10_prime, _11, _11_prime, _12, _12_prime,
       _13, _13_prime, _14, _14_prime, _15, _15_prime, _16, _16_prime, _17, _17_prime, _18, _18_prime, _19,
       _19_prime, _20, _20_prime, _21, _21_prime, _22, _22_prime, _23, _23_prime, _24, _24_prime, _25,
       _25_prime, _26, _26_prime, _27, _27_prime, _28, _28_prime, _29, _29_prime, _30, _30_prime, _31,
       _31_prime;

  Register #(.width(32)) register_1 (.D(_0), .Q(_0_prime), .clk(clk));  // open: en, clr
  Register #(.width(32)) register_2 (.D(_8), .Q(_8_prime), .clk(clk));  // open: en, clr
  Register #(.width(32)) register_3 (.D(_16), .Q(_16_prime), .clk(clk));  // open: en, clr
  Register #(.width(32)) register_4 (.D(_24), .Q(_24_prime), .clk(clk));  // open: en, clr
  Register #(.width(32)) register_5 (.D(_1), .Q(_1_prime), .clk(clk));  // open: en, clr
  Register #(.width(32)) register_6 (.D(_9), .Q(_9_prime), .clk(clk));  // open: en, clr
  Register #(.width(32)) register_7 (.D(_17), .Q(_17_prime), .clk(clk));  // open: en, clr
  Register #(.width(32)) register_8 (.D(_25), .Q(_25_prime), .clk(clk));  // open: en, clr
  Register #(.width(32)) register_9 (.D(_2), .Q(_2_prime), .clk(clk));  // open: en, clr
  Register #(.width(32)) register_10 (.D(_10), .Q(_10_prime), .clk(clk));  // open: en, clr
  Register #(.width(32)) register_11 (.D(_18), .Q(_18_prime), .clk(clk));  // open: en, clr
  Register #(.width(32)) register_12 (.D(_26), .Q(_26_prime), .clk(clk));  // open: en, clr
  Register #(.width(32)) register_13 (.D(_3), .Q(_3_prime), .clk(clk));  // open: en, clr
  Register #(.width(32)) register_14 (.D(_11), .Q(_11_prime), .clk(clk));  // open: en, clr
  Register #(.width(32)) register_15 (.D(_19), .Q(_19_prime), .clk(clk));  // open: en, clr
  Register #(.width(32)) register_16 (.D(_27), .Q(_27_prime), .clk(clk));  // open: en, clr
  Register #(.width(32)) register_17 (.D(_4), .Q(_4_prime), .clk(clk));  // open: en, clr
  Register #(.width(32)) register_18 (.D(_12), .Q(_12_prime), .clk(clk));  // open: en, clr
  Register #(.width(32)) register_19 (.D(_20), .Q(_20_prime), .clk(clk));  // open: en, clr
  Register #(.width(32)) register_20 (.D(_28), .Q(_28_prime), .clk(clk));  // open: en, clr
  Register #(.width(32)) register_21 (.D(_5), .Q(_5_prime), .clk(clk));  // open: en, clr
  Register #(.width(32)) register_22 (.D(_13), .Q(_13_prime), .clk(clk));  // open: en, clr
  Register #(.width(32)) register_23 (.D(_21), .Q(_21_prime), .clk(clk));  // open: en, clr
  Register #(.width(32)) register_24 (.D(_29), .Q(_29_prime), .clk(clk));  // open: en, clr
  Register #(.width(32)) register_25 (.D(_6), .Q(_6_prime), .clk(clk));  // open: en, clr
  Register #(.width(32)) register_26 (.D(_14), .Q(_14_prime), .clk(clk));  // open: en, clr
  Register #(.width(32)) register_27 (.D(_22), .Q(_22_prime), .clk(clk));  // open: en, clr
  Register #(.width(32)) register_28 (.D(_30), .Q(_30_prime), .clk(clk));  // open: en, clr
  Register #(.width(32)) register_29 (.D(_7), .Q(_7_prime), .clk(clk));  // open: en, clr
  Register #(.width(32)) register_30 (.D(_15), .Q(_15_prime), .clk(clk));  // open: en, clr
  Register #(.width(32)) register_31 (.D(_23), .Q(_23_prime), .clk(clk));  // open: en, clr
  Register #(.width(32)) register_32 (.D(_31), .Q(_31_prime), .clk(clk));  // open: en, clr
endmodule

module registers2 (
  input  in_1,
  input  [31:0] in_2,
  input  [31:0] in_3,
  input  [31:0] in_4,
  input  [31:0] in_5,
  input  [31:0] in_6,
  input  [31:0] in_7,
  input  [31:0] in_8,
  input  [31:0] in_9,
  input  [31:0] in_10,
  input  [31:0] in_11,
  input  [31:0] in_12,
  input  [31:0] in_13,
  input  [31:0] in_14,
  input  [31:0] in_15,
  input  [31:0] in_16,
  input  [31:0] in_17,
  input  [31:0] in_18,
  input  [31:0] in_19,
  input  [31:0] in_20,
  input  [31:0] in_21,
  input  [31:0] in_22,
  input  [31:0] in_23,
  input  [31:0] in_24,
  input  [31:0] in_25,
  input  [31:0] in_26,
  input  [31:0] in_27,
  input  [31:0] in_28,
  input  [31:0] in_29,
  input  [31:0] in_30,
  input  [31:0] in_31,
  input  [31:0] in_32,
  input  [31:0] in_33,
  output [31:0] out_34,
  output [31:0] out_35,
  output [31:0] out_36,
  output [31:0] out_37,
  output [31:0] out_38,
  output [31:0] out_39,
  output [31:0] out_40,
  output [31:0] out_41,
  output [31:0] out_42,
  output [31:0] out_43,
  output [31:0] out_44,
  output [31:0] out_45,
  output [31:0] out_46,
  output [31:0] out_47,
  output [31:0] out_48,
  output [31:0] out_49,
  output [31:0] out_50,
  output [31:0] out_51,
  output [31:0] out_52,
  output [31:0] out_53,
  output [31:0] out_54,
  output [31:0] out_55,
  output [31:0] out_56,
  output [31:0] out_57,
  output [31:0] out_58,
  output [31:0] out_59,
  output [31:0] out_60,
  output [31:0] out_61,
  output [31:0] out_62,
  output [31:0] out_63,
  output [31:0] out_64,
  output [31:0] out_65
);

  Register #(.width(32)) register_1 (.D(in_2), .Q(out_34), .clk(in_1));  // open: en, clr
  Register #(.width(32)) register_2 (.D(in_6), .Q(out_38), .clk(in_1));  // open: en, clr
  Register #(.width(32)) register_3 (.D(in_10), .Q(out_42), .clk(in_1));  // open: en, clr
  Register #(.width(32)) register_4 (.D(in_14), .Q(out_46), .clk(in_1));  // open: en, clr
  Register #(.width(32)) register_5 (.D(in_18), .Q(out_50), .clk(in_1));  // open: en, clr
  Register #(.width(32)) register_6 (.D(in_22), .Q(out_54), .clk(in_1));  // open: en, clr
  Register #(.width(32)) register_7 (.D(in_26), .Q(out_58), .clk(in_1));  // open: en, clr
  Register #(.width(32)) register_8 (.D(in_30), .Q(out_62), .clk(in_1));  // open: en, clr
  Register #(.width(32)) register_9 (.D(in_3), .Q(out_35), .clk(in_1));  // open: en, clr
  Register #(.width(32)) register_10 (.D(in_7), .Q(out_39), .clk(in_1));  // open: en, clr
  Register #(.width(32)) register_11 (.D(in_11), .Q(out_43), .clk(in_1));  // open: en, clr
  Register #(.width(32)) register_12 (.D(in_15), .Q(out_47), .clk(in_1));  // open: en, clr
  Register #(.width(32)) register_13 (.D(in_19), .Q(out_51), .clk(in_1));  // open: en, clr
  Register #(.width(32)) register_14 (.D(in_23), .Q(out_55), .clk(in_1));  // open: en, clr
  Register #(.width(32)) register_15 (.D(in_27), .Q(out_59), .clk(in_1));  // open: en, clr
  Register #(.width(32)) register_16 (.D(in_31), .Q(out_63), .clk(in_1));  // open: en, clr
  Register #(.width(32)) register_17 (.D(in_4), .Q(out_36), .clk(in_1));  // open: en, clr
  Register #(.width(32)) register_18 (.D(in_8), .Q(out_40), .clk(in_1));  // open: en, clr
  Register #(.width(32)) register_19 (.D(in_12), .Q(out_44), .clk(in_1));  // open: en, clr
  Register #(.width(32)) register_20 (.D(in_16), .Q(out_48), .clk(in_1));  // open: en, clr
  Register #(.width(32)) register_21 (.D(in_20), .Q(out_52), .clk(in_1));  // open: en, clr
  Register #(.width(32)) register_22 (.D(in_24), .Q(out_56), .clk(in_1));  // open: en, clr
  Register #(.width(32)) register_23 (.D(in_28), .Q(out_60), .clk(in_1));  // open: en, clr
  Register #(.width(32)) register_24 (.D(in_32), .Q(out_64), .clk(in_1));  // open: en, clr
  Register #(.width(32)) register_25 (.D(in_5), .Q(out_37), .clk(in_1));  // open: en, clr
  Register #(.width(32)) register_26 (.D(in_9), .Q(out_41), .clk(in_1));  // open: en, clr
  Register #(.width(32)) register_27 (.D(in_13), .Q(out_45), .clk(in_1));  // open: en, clr
  Register #(.width(32)) register_28 (.D(in_17), .Q(out_49), .clk(in_1));  // open: en, clr
  Register #(.width(32)) register_29 (.D(in_21), .Q(out_53), .clk(in_1));  // open: en, clr
  Register #(.width(32)) register_30 (.D(in_25), .Q(out_57), .clk(in_1));  // open: en, clr
  Register #(.width(32)) register_31 (.D(in_29), .Q(out_61), .clk(in_1));  // open: en, clr
  Register #(.width(32)) register_32 (.D(in_33), .Q(out_65), .clk(in_1));  // open: en, clr

  // Other names for the same wires on the sheet: clk = in_1
endmodule

module registers3 (
  input  [31:0] in_1,
  input  [31:0] in_2,
  input  [31:0] in_3,
  input  [31:0] in_4,
  input  [31:0] in_5,
  input  [31:0] in_6,
  input  [31:0] in_7,
  input  [31:0] in_8,
  input  [31:0] in_9,
  input  [31:0] in_10,
  input  [31:0] in_11,
  input  [31:0] in_12,
  input  [31:0] in_13,
  input  [31:0] in_14,
  input  [31:0] in_15,
  input  [31:0] in_16,
  input  [31:0] in_17,
  input  [31:0] in_18,
  input  [31:0] in_19,
  input  [31:0] in_20,
  input  [31:0] in_21,
  input  [31:0] in_22,
  input  [31:0] in_23,
  input  [31:0] in_24,
  input  [31:0] in_25,
  input  [31:0] in_26,
  input  [31:0] in_27,
  input  [31:0] in_28,
  input  [31:0] in_29,
  input  [31:0] in_30,
  input  [31:0] in_31,
  input  [31:0] in_32,
  input  in_33,
  output [31:0] out_34,
  output [31:0] out_35,
  output [31:0] out_36,
  output [31:0] out_37,
  output [31:0] out_38,
  output [31:0] out_39,
  output [31:0] out_40,
  output [31:0] out_41,
  output [31:0] out_42,
  output [31:0] out_43,
  output [31:0] out_44,
  output [31:0] out_45,
  output [31:0] out_46,
  output [31:0] out_47,
  output [31:0] out_48,
  output [31:0] out_49,
  output [31:0] out_50,
  output [31:0] out_51,
  output [31:0] out_52,
  output [31:0] out_53,
  output [31:0] out_54,
  output [31:0] out_55,
  output [31:0] out_56,
  output [31:0] out_57,
  output [31:0] out_58,
  output [31:0] out_59,
  output [31:0] out_60,
  output [31:0] out_61,
  output [31:0] out_62,
  output [31:0] out_63,
  output [31:0] out_64,
  output [31:0] out_65
);

  Register #(.width(32)) register_1 (.D(in_1), .Q(out_34), .clk(in_33));  // open: en, clr
  Register #(.width(32)) register_2 (.D(in_5), .Q(out_38), .clk(in_33));  // open: en, clr
  Register #(.width(32)) register_3 (.D(in_9), .Q(out_42), .clk(in_33));  // open: en, clr
  Register #(.width(32)) register_4 (.D(in_13), .Q(out_46), .clk(in_33));  // open: en, clr
  Register #(.width(32)) register_5 (.D(in_17), .Q(out_50), .clk(in_33));  // open: en, clr
  Register #(.width(32)) register_6 (.D(in_21), .Q(out_54), .clk(in_33));  // open: en, clr
  Register #(.width(32)) register_7 (.D(in_25), .Q(out_58), .clk(in_33));  // open: en, clr
  Register #(.width(32)) register_8 (.D(in_29), .Q(out_62), .clk(in_33));  // open: en, clr
  Register #(.width(32)) register_9 (.D(in_2), .Q(out_35), .clk(in_33));  // open: en, clr
  Register #(.width(32)) register_10 (.D(in_6), .Q(out_39), .clk(in_33));  // open: en, clr
  Register #(.width(32)) register_11 (.D(in_10), .Q(out_43), .clk(in_33));  // open: en, clr
  Register #(.width(32)) register_12 (.D(in_14), .Q(out_47), .clk(in_33));  // open: en, clr
  Register #(.width(32)) register_13 (.D(in_18), .Q(out_51), .clk(in_33));  // open: en, clr
  Register #(.width(32)) register_14 (.D(in_22), .Q(out_55), .clk(in_33));  // open: en, clr
  Register #(.width(32)) register_15 (.D(in_26), .Q(out_59), .clk(in_33));  // open: en, clr
  Register #(.width(32)) register_16 (.D(in_30), .Q(out_63), .clk(in_33));  // open: en, clr
  Register #(.width(32)) register_17 (.D(in_3), .Q(out_36), .clk(in_33));  // open: en, clr
  Register #(.width(32)) register_18 (.D(in_7), .Q(out_40), .clk(in_33));  // open: en, clr
  Register #(.width(32)) register_19 (.D(in_11), .Q(out_44), .clk(in_33));  // open: en, clr
  Register #(.width(32)) register_20 (.D(in_15), .Q(out_48), .clk(in_33));  // open: en, clr
  Register #(.width(32)) register_21 (.D(in_19), .Q(out_52), .clk(in_33));  // open: en, clr
  Register #(.width(32)) register_22 (.D(in_23), .Q(out_56), .clk(in_33));  // open: en, clr
  Register #(.width(32)) register_23 (.D(in_27), .Q(out_60), .clk(in_33));  // open: en, clr
  Register #(.width(32)) register_24 (.D(in_31), .Q(out_64), .clk(in_33));  // open: en, clr
  Register #(.width(32)) register_25 (.D(in_4), .Q(out_37), .clk(in_33));  // open: en, clr
  Register #(.width(32)) register_26 (.D(in_8), .Q(out_41), .clk(in_33));  // open: en, clr
  Register #(.width(32)) register_27 (.D(in_12), .Q(out_45), .clk(in_33));  // open: en, clr
  Register #(.width(32)) register_28 (.D(in_16), .Q(out_49), .clk(in_33));  // open: en, clr
  Register #(.width(32)) register_29 (.D(in_20), .Q(out_53), .clk(in_33));  // open: en, clr
  Register #(.width(32)) register_30 (.D(in_24), .Q(out_57), .clk(in_33));  // open: en, clr
  Register #(.width(32)) register_31 (.D(in_28), .Q(out_61), .clk(in_33));  // open: en, clr
  Register #(.width(32)) register_32 (.D(in_32), .Q(out_65), .clk(in_33));  // open: en, clr

  // Other names for the same wires on the sheet: clk = in_33
endmodule
